# Fritzing sketch Eye Tracking NodeMCU (saved by Fritzing 0.9.3b)
breadboards: 1

parts:
  U1 = NodeMCU V1.0
  U2 = 2-Channel 5v Relay Shield [package=relay-2ch5v10a]
  Power_plug1 = Power plug

nets:
  N1: U1.D0, U2.IN1
  N2: U1.D1, U2.IN2
  GND: U1.GND, U2.GND, Power_plug1.GND
  VCC: U1.Vin, U2.VCC, Power_plug1.VCC

custom parts:
  NodeMCU V1.0: ESP8266 based NodeMCU
  2-Channel 5v Relay Shield: 2 Channel 5v Relay Shield w. 2x SPD-06VDC-SD-C
